// Logisim project Circuito tonyn.circ as structural Verilog: 3 circuits, main circuit main
module main (
  input  A,
  input  B,
  input  C,
  input  A_2,
  input  B_2,
  input  C_2,
  output S,
  output S_2
);

  Exemplo exemplo_1 (.A(A), .B(B), .C(C), .out_4(S));
  // Exemplo2 exemplo2_1: pin names not known; wires that end beside it: A_2, B_2, C_2, S_2
endmodule

module Exemplo (
  input  A,
  input  B,
  input  C,
  output out_4
);

  wire not_1_out, not_2_out, or_1_out, xor_1_out;

  xor xor_1 (xor_1_out, A, B);
  not not_1 (not_1_out, A);
  or or_1 (or_1_out, xor_1_out, not_1_out);
  not not_2 (not_2_out, C);
  and and_1 (out_4, or_1_out, not_2_out);
endmodule

module Exemplo2 (
  input  A,
  input  B,
  input  C,
  output out_4
);

  wire and_1_out, or_1_out, xor_1_out;

  xor xor_1 (xor_1_out, A, B);
  or or_1 (or_1_out, xor_1_out, ~B);  // OR_Gate
  and and_1 (and_1_out, or_1_out, ~A);  // AND_Gate
  or or_2 (out_4, and_1_out, ~C);  // OR_Gate
endmodule
